// Logisim project ABC.circ as structural Verilog
module B (
  input  a,
  input  b,
  input  c,
  input  d,
  output B_1,
  output B_2,
  output B_3,
  output B_4,
  output B_5,
  output B_6,
  output B_7,
  output B_8
);

  wire and_1_out, and_2_out, and_3_out, and_4_out, and_5_out, and_6_out, and_7_out, and_8_out, and_9_out,
       and_10_out, and_11_out, and_12_out, and_13_out, and_14_out, and_15_out, and_16_out, and_17_out,
       and_18_out, and_19_out, and_20_out, and_21_out, and_22_out, and_23_out, not_1_out, not_2_out,
       not_3_out, not_4_out, not_5_out, not_6_out, not_7_out, not_8_out, not_9_out, not_10_out, not_11_out,
       not_12_out, not_13_out, not_14_out, not_15_out, not_16_out, not_17_out, not_18_out, not_19_out,
       not_20_out, not_21_out, not_22_out, not_23_out, not_24_out, not_25_out, not_26_out, not_27_out,
       not_28_out, not_29_out, not_30_out, not_31_out, not_32_out, not_33_out, not_34_out, not_35_out,
       not_36_out, not_37_out, not_38_out, not_39_out, not_40_out, not_41_out;

  not not_1 (not_1_out, a);
  not not_2 (not_2_out, b);
  not not_3 (not_3_out, b);
  not not_4 (not_4_out, d);
  not not_5 (not_5_out, c);
  not not_6 (not_6_out, d);
  not not_7 (not_7_out, c);
  and and_1 (and_1_out, b, not_7_out, not_8_out);
  not not_8 (not_8_out, d);
  not not_9 (not_9_out, b);
  and and_2 (and_2_out, not_9_out, c, d);
  not not_10 (not_10_out, a);
  not not_11 (not_11_out, c);
  not not_12 (not_12_out, d);
  not not_13 (not_13_out, a);
  not not_14 (not_14_out, b);
  not not_15 (not_15_out, b);
  not not_16 (not_16_out, d);
  not not_17 (not_17_out, c);
  not not_18 (not_18_out, a);
  not not_19 (not_19_out, b);
  not not_20 (not_20_out, b);
  not not_21 (not_21_out, d);
  not not_22 (not_22_out, c);
  not not_23 (not_23_out, a);
  not not_24 (not_24_out, b);
  not not_25 (not_25_out, d);
  not not_26 (not_26_out, b);
  not not_27 (not_27_out, c);
  not not_28 (not_28_out, a);
  not not_29 (not_29_out, c);
  not not_30 (not_30_out, c);
  not not_31 (not_31_out, d);
  not not_32 (not_32_out, b);
  not not_33 (not_33_out, d);
  not not_34 (not_34_out, b);
  and and_3 (and_3_out, not_34_out, c, not_35_out);
  not not_35 (not_35_out, d);
  not not_36 (not_36_out, c);
  and and_4 (and_4_out, b, not_36_out, d);
  not not_37 (not_37_out, a);
  not not_38 (not_38_out, c);
  not not_39 (not_39_out, c);
  not not_40 (not_40_out, d);
  not not_41 (not_41_out, b);
  and and_5 (and_5_out, not_1_out, not_2_out, c, d);
  or or_1 (B_1, and_5_out, and_6_out, and_7_out);
  and and_6 (and_6_out, a, not_3_out, c, not_4_out);
  and and_7 (and_7_out, b, not_5_out, not_6_out);
  or or_2 (B_2, and_1_out, and_2_out);
  and and_8 (and_8_out, not_10_out, b, not_11_out, not_12_out);
  and and_9 (and_9_out, not_13_out, not_14_out, c, d);
  and and_10 (and_10_out, a, not_15_out, c, not_16_out);
  and and_11 (and_11_out, a, b, not_17_out, d);
  and and_12 (and_12_out, not_18_out, not_19_out, c, d);
  and and_13 (and_13_out, a, not_20_out, c, not_21_out);
  or or_3 (B_4, and_12_out, and_13_out, and_14_out);
  and and_14 (and_14_out, b, not_22_out, d);
  and and_15 (and_15_out, not_23_out, not_24_out, c, not_25_out);
  or or_4 (B_5, and_15_out, and_16_out, and_17_out);
  and and_16 (and_16_out, a, not_26_out, c, d);
  and and_17 (and_17_out, b, not_27_out, d);
  and and_18 (and_18_out, not_28_out, b, not_29_out, d);
  or or_5 (B_6, and_18_out, and_19_out, and_20_out);
  and and_19 (and_19_out, a, b, not_30_out, not_31_out);
  and and_20 (and_20_out, not_32_out, c, not_33_out);
  or or_6 (B_7, and_3_out, and_4_out);
  and and_21 (and_21_out, not_37_out, b, not_38_out, d);
  or or_7 (B_8, and_21_out, and_22_out, and_23_out);
  and and_22 (and_22_out, a, b, not_39_out, not_40_out);
  and and_23 (and_23_out, not_41_out, c, d);
  or or_8 (B_3, and_8_out, and_9_out, and_10_out, and_11_out);
endmodule

module A (
  input  a,
  input  b,
  input  c,
  input  d,
  output A_1,
  output A_2,
  output A_3,
  output A_4,
  output A_5,
  output A_6,
  output A_7,
  output A_8,
  output A_9
);

  wire and_1_out, and_2_out, and_3_out, and_4_out, and_5_out, and_6_out, and_7_out, and_8_out, and_9_out,
       and_10_out, and_11_out, and_12_out, and_13_out, and_14_out, and_15_out, and_16_out, and_17_out,
       and_18_out, and_19_out, and_20_out, and_21_out, and_22_out, and_23_out, and_24_out, and_25_out,
       and_26_out, and_27_out, and_28_out, and_29_out, not_1_out, not_2_out, not_3_out, not_4_out, not_5_out,
       not_6_out, not_7_out, not_8_out, not_9_out, not_10_out, not_11_out, not_12_out, not_13_out,
       not_14_out, not_15_out, not_16_out, not_17_out, not_18_out, not_19_out, not_20_out, not_21_out,
       not_22_out, not_23_out, not_24_out, not_25_out, not_26_out, not_27_out, not_28_out, not_29_out,
       not_30_out, not_31_out, not_32_out, not_33_out, not_34_out, not_35_out, not_36_out, not_37_out,
       not_38_out, not_39_out, not_40_out, not_41_out, not_42_out, not_43_out, not_44_out, not_45_out;

  not not_1 (not_1_out, a);
  not not_2 (not_2_out, d);
  not not_3 (not_3_out, b);
  not not_4 (not_4_out, c);
  not not_5 (not_5_out, b);
  not not_6 (not_6_out, d);
  not not_7 (not_7_out, c);
  not not_8 (not_8_out, d);
  not not_9 (not_9_out, a);
  not not_10 (not_10_out, b);
  not not_11 (not_11_out, c);
  not not_12 (not_12_out, d);
  not not_13 (not_13_out, a);
  not not_14 (not_14_out, d);
  not not_15 (not_15_out, c);
  not not_16 (not_16_out, b);
  not not_17 (not_17_out, d);
  not not_18 (not_18_out, b);
  not not_19 (not_19_out, d);
  not not_20 (not_20_out, a);
  not not_21 (not_21_out, c);
  not not_22 (not_22_out, b);
  not not_23 (not_23_out, c);
  not not_24 (not_24_out, d);
  not not_25 (not_25_out, a);
  not not_26 (not_26_out, b);
  not not_27 (not_27_out, c);
  not not_28 (not_28_out, a);
  not not_29 (not_29_out, c);
  not not_30 (not_30_out, b);
  not not_31 (not_31_out, d);
  not not_32 (not_32_out, a);
  not not_33 (not_33_out, b);
  not not_34 (not_34_out, d);
  not not_35 (not_35_out, c);
  not not_36 (not_36_out, d);
  not not_37 (not_37_out, a);
  not not_38 (not_38_out, d);
  not not_39 (not_39_out, b);
  not not_40 (not_40_out, c);
  not not_41 (not_41_out, d);
  not not_42 (not_42_out, c);
  not not_43 (not_43_out, d);
  not not_44 (not_44_out, a);
  not not_45 (not_45_out, b);
  and and_1 (and_1_out, not_1_out, b, c, not_2_out);
  and and_2 (and_2_out, a, not_3_out, not_4_out, d);
  and and_3 (and_3_out, a, not_5_out, c, not_6_out);
  and and_4 (and_4_out, a, b, not_7_out, not_8_out);
  and and_5 (and_5_out, not_9_out, b, c, d);
  and and_6 (and_6_out, a, not_10_out, c, d);
  or or_1 (A_2, and_5_out, and_6_out, and_7_out);
  and and_7 (and_7_out, a, not_11_out, not_12_out);
  and and_8 (and_8_out, not_13_out, b, c, not_14_out);
  and and_9 (and_9_out, a, b, not_15_out, d);
  or or_2 (A_3, and_8_out, and_9_out, and_10_out);
  and and_10 (and_10_out, a, not_16_out, not_17_out);
  and and_11 (and_11_out, a, not_18_out, c, not_19_out);
  and and_12 (and_12_out, not_20_out, b, c, d);
  or or_3 (A_4, and_11_out, and_12_out, and_13_out);
  and and_13 (and_13_out, a, not_21_out, d);
  and and_14 (and_14_out, a, not_22_out, not_23_out, not_24_out);
  and and_15 (and_15_out, not_25_out, b, c, d);
  and and_16 (and_16_out, a, not_26_out, c, d);
  and and_17 (and_17_out, a, b, not_27_out, d);
  and and_18 (and_18_out, not_28_out, b, c, d);
  and and_19 (and_19_out, a, b, not_29_out, d);
  or or_4 (A_6, and_18_out, and_19_out, and_20_out);
  and and_20 (and_20_out, a, not_30_out, not_31_out);
  and and_21 (and_21_out, not_32_out, b, c, d);
  and and_22 (and_22_out, a, not_33_out, not_34_out);
  or or_5 (A_7, and_21_out, and_22_out, and_23_out);
  and and_23 (and_23_out, a, not_35_out, not_36_out);
  and and_24 (and_24_out, not_37_out, b, c, not_38_out);
  and and_25 (and_25_out, a, not_39_out, c, d);
  or or_6 (A_8, and_24_out, and_25_out, and_26_out);
  and and_26 (and_26_out, a, not_40_out, not_41_out);
  and and_27 (and_27_out, a, b, not_42_out, not_43_out);
  and and_28 (and_28_out, not_44_out, b, c, d);
  or or_7 (A_9, and_27_out, and_28_out, and_29_out);
  and and_29 (and_29_out, a, not_45_out, d);
  or or_8 (A_1, and_1_out, and_2_out, and_3_out, and_4_out);
  or or_9 (A_5, and_14_out, and_15_out, and_16_out, and_17_out);
endmodule

module C (
  input  a,
  input  b,
  input  c,
  input  d,
  output C_1,
  output C_2,
  output C_3,
  output C_4,
  output C_5,
  output C_6,
  output C_7
);

  wire and_2_out, and_3_out, and_4_out, and_5_out, and_6_out, and_7_out, and_8_out, and_9_out, and_10_out,
       and_11_out, and_12_out, and_13_out, and_14_out, and_15_out, and_16_out, and_17_out, and_18_out,
       and_19_out, not_1_out, not_2_out, not_3_out, not_4_out, not_5_out, not_6_out, not_7_out, not_8_out,
       not_9_out, not_10_out, not_11_out, not_12_out, not_13_out, not_14_out, not_15_out, not_16_out,
       not_17_out, not_18_out, not_19_out, not_20_out, not_21_out, not_22_out, not_23_out, not_24_out,
       not_25_out, not_26_out, not_27_out, not_28_out, not_29_out, not_30_out, not_31_out, not_32_out,
       not_33_out, not_34_out, not_35_out, not_36_out, not_37_out, not_38_out, not_39_out, not_40_out,
       not_41_out, not_42_out, not_43_out;

  not not_1 (not_1_out, b);
  not not_2 (not_2_out, c);
  not not_3 (not_3_out, a);
  not not_4 (not_4_out, c);
  not not_5 (not_5_out, d);
  not not_6 (not_6_out, c);
  not not_7 (not_7_out, d);
  not not_8 (not_8_out, c);
  and and_1 (C_2, not_8_out, not_9_out);
  not not_9 (not_9_out, d);
  not not_10 (not_10_out, c);
  not not_11 (not_11_out, a);
  not not_12 (not_12_out, c);
  not not_13 (not_13_out, d);
  not not_14 (not_14_out, b);
  not not_15 (not_15_out, c);
  not not_16 (not_16_out, d);
  not not_17 (not_17_out, a);
  not not_18 (not_18_out, b);
  not not_19 (not_19_out, c);
  not not_20 (not_20_out, d);
  not not_21 (not_21_out, c);
  not not_22 (not_22_out, c);
  not not_23 (not_23_out, b);
  and and_2 (and_2_out, not_23_out, not_24_out, not_25_out);
  not not_24 (not_24_out, c);
  not not_25 (not_25_out, d);
  not not_26 (not_26_out, c);
  and and_3 (and_3_out, b, not_26_out, d);
  not not_27 (not_27_out, a);
  not not_28 (not_28_out, c);
  not not_29 (not_29_out, b);
  not not_30 (not_30_out, c);
  not not_31 (not_31_out, d);
  not not_32 (not_32_out, c);
  not not_33 (not_33_out, d);
  not not_34 (not_34_out, c);
  not not_35 (not_35_out, d);
  not not_36 (not_36_out, b);
  not not_37 (not_37_out, c);
  not not_38 (not_38_out, a);
  not not_39 (not_39_out, c);
  not not_40 (not_40_out, a);
  not not_41 (not_41_out, b);
  not not_42 (not_42_out, c);
  not not_43 (not_43_out, d);
  and and_4 (and_4_out, a, not_1_out, not_2_out, d);
  or or_1 (C_1, and_4_out, and_5_out, and_6_out);
  and and_5 (and_5_out, not_3_out, not_4_out, not_5_out);
  and and_6 (and_6_out, b, not_6_out, not_7_out);
  and and_7 (and_7_out, a, b, not_10_out, d);
  and and_8 (and_8_out, not_11_out, not_12_out, not_13_out);
  or or_2 (C_3, and_7_out, and_8_out, and_9_out);
  and and_9 (and_9_out, not_14_out, not_15_out, not_16_out);
  and and_10 (and_10_out, not_17_out, not_18_out, not_19_out, not_20_out);
  or or_3 (C_4, and_10_out, and_11_out, and_12_out);
  and and_11 (and_11_out, b, not_21_out, d);
  and and_12 (and_12_out, a, not_22_out, d);
  or or_4 (C_5, and_2_out, and_3_out);
  and and_13 (and_13_out, not_27_out, b, not_28_out, d);
  and and_14 (and_14_out, not_29_out, not_30_out, not_31_out);
  or or_5 (C_6, and_13_out, and_14_out, and_15_out);
  and and_15 (and_15_out, a, not_32_out, not_33_out);
  and and_16 (and_16_out, a, b, not_34_out, not_35_out);
  and and_17 (and_17_out, a, not_36_out, not_37_out, d);
  and and_18 (and_18_out, not_38_out, b, not_39_out, d);
  and and_19 (and_19_out, not_40_out, not_41_out, not_42_out, not_43_out);
  or or_6 (C_7, and_16_out, and_17_out, and_18_out, and_19_out);
endmodule
