// Logisim project after_mux.circ as structural Verilog: 1 circuit, main circuit main
module main (
  input  CLK,
  input  top_and_1,
  input  top_and_2,
  input  top_and_3,
  input  top_and_4,
  input  bot_and_1,
  input  bot_and_2,
  input  bot_and_3,
  input  bot_and_4,
  output OUTPUT,
  output C_3,
  output C_2,
  output C_1,
  output C_0
);

  wire and_1_out, and_2_out, and_3_out, and_4_out, and_5_out, and_6_out, and_7_out, and_8_out, and_9_out,
       and_10_out, and_12_out, buffer_1_out, controlled_buffer_1_out, not_1_out, not_2_out, not_3_out,
       not_4_out, not_5_out, or_1_out, or_2_out, or_3_out, undriven;

  and and_1 (and_1_out, top_and_1, top_and_2, top_and_3, top_and_4);
  and and_2 (and_2_out, bot_and_1, bot_and_2, bot_and_3, bot_and_4);
  assign controlled_buffer_1_out = or_1_out ? and_1_out : 1'bz;  // Controlled_Buffer controlled_buffer_1
  assign controlled_buffer_1_out = not_1_out ? and_2_out : 1'bz;  // Controlled_Buffer controlled_buffer_2
  not not_1 (not_1_out, or_1_out);
  or or_1 (or_1_out, or_3_out, or_2_out);
  or or_2 (or_2_out, and_3_out, and_4_out, and_5_out, and_6_out);
  or or_3 (or_3_out, and_7_out, and_8_out, and_9_out, and_10_out);
  buf buffer_1 (buffer_1_out, controlled_buffer_1_out);
  and and_3 (and_3_out, not_2_out, not_3_out, not_4_out, not_5_out);
  and and_4 (and_4_out, C_0, not_3_out, not_4_out, not_5_out);
  and and_5 (and_5_out, C_1, not_2_out, not_4_out, not_5_out);
  and and_6 (and_6_out, C_0, C_2, not_3_out, not_5_out);
  and and_7 (and_7_out, C_0, C_1, C_2, not_5_out);
  and and_8 (and_8_out, C_3, not_2_out, not_3_out, not_4_out);
  and and_9 (and_9_out, C_3, C_2, C_0, not_3_out);
  and and_10 (and_10_out, C_3, C_2, C_1, not_2_out);
  reset_handler_main main_1 (.in_1(buffer_1_out), .in_2(CLK));  // open: out_3
  J_K_Flip_Flop j_k_ff_1 (
    .J(1'b1), .clk(buffer_1_out), .K(1'b1), .Q(C_0), .en(1'b1), .reset(undriven));  // open: Qn, preset
  not not_2 (not_2_out, C_0);
  J_K_Flip_Flop j_k_ff_2 (.J(1'b1), .clk(C_0), .K(1'b1), .Q(C_1), .en(1'b1), .reset(undriven));  // open: Qn, preset
  not not_3 (not_3_out, C_1);
  J_K_Flip_Flop j_k_ff_3 (.J(1'b1), .clk(C_2), .K(1'b1), .Q(C_3), .en(1'b1), .reset(undriven));  // open: Qn, preset
  J_K_Flip_Flop j_k_ff_4 (.J(1'b1), .clk(C_1), .K(1'b1), .Q(C_2), .en(1'b1), .reset(undriven));  // open: Qn, preset
  not not_4 (not_4_out, C_2);
  not not_5 (not_5_out, C_3);
  and and_11 (OUTPUT, buffer_1_out, and_12_out);
  and and_12 (and_12_out, C_3, C_2, C_1, C_0);

  // Notes on the sheet:
  //   Reset handler is not connected
  //   Since it is not needed
endmodule
