// Logisim project final.circ as structural Verilog: 1 circuit, main circuit main
module main (
  input  in_1
);

  wire a_1_a_1, a_1_a_2, a_1_a_3, a_1_a_4, a_1_a_5, a_1_a_6, a_1_a_7, a_1_a_8, a_1_a_9, b_1_b_1, b_1_b_2,
       b_1_b_3, b_1_b_4, b_1_b_5, b_1_b_6, b_1_b_7, b_1_b_8, c_1_c_1, c_1_c_2, c_1_c_3, c_1_c_4, c_1_c_5,
       c_1_c_6, c_1_c_7, clock_1_out, d_ff_1_q, d_ff_2_q, d_ff_3_q, main_1_output, multiplexer_1_out,
       multiplexer_2_out, multiplexer_3_out, not_1_out;
  wire [3:0] main_1_c_0;

  Clock clock_1 (.out(clock_1_out));
  not not_1 (not_1_out, in_1);
  A a_1 (
    .a(d_ff_1_q), .b(d_ff_2_q), .c(d_ff_3_q), .d(in_1), .A_1(a_1_a_1), .A_2(a_1_a_2), .A_3(a_1_a_3),
    .A_4(a_1_a_4), .A_5(a_1_a_5), .A_6(a_1_a_6), .A_7(a_1_a_7), .A_8(a_1_a_8), .A_9(a_1_a_9));
  B b_1 (
    .a(d_ff_1_q), .b(d_ff_2_q), .c(d_ff_3_q), .d(in_1), .B_1(b_1_b_1), .B_2(b_1_b_2), .B_3(b_1_b_3),
    .B_4(b_1_b_4), .B_5(b_1_b_5), .B_6(b_1_b_6), .B_7(b_1_b_7), .B_8(b_1_b_8));
  C c_1 (
    .a(d_ff_1_q), .b(d_ff_2_q), .c(d_ff_3_q), .d(in_1), .C_1(c_1_c_1), .C_2(c_1_c_2), .C_3(c_1_c_3),
    .C_4(c_1_c_4), .C_5(c_1_c_5), .C_6(c_1_c_6), .C_7(c_1_c_7));
  Multiplexer #(.select(4)) multiplexer_1 (
    .in0(a_1_a_1), .in1(a_1_a_2), .in2(a_1_a_3), .in3(a_1_a_4), .in4(a_1_a_5), .in5(a_1_a_6), .in6(a_1_a_7),
    .in7(a_1_a_5), .in8(a_1_a_5), .in9(a_1_a_6), .in10(a_1_a_6), .in11(a_1_a_6), .in12(a_1_a_6),
    .in13(a_1_a_6), .in14(a_1_a_8), .in15(a_1_a_9), .out(multiplexer_1_out), .sel(main_1_c_0), .en(1'b1));
  Multiplexer #(.select(4)) multiplexer_2 (
    .in0(b_1_b_1), .in1(b_1_b_2), .in2(b_1_b_3), .in3(b_1_b_4), .in4(b_1_b_5), .in5(b_1_b_4), .in6(b_1_b_6),
    .in7(b_1_b_5), .in8(b_1_b_5), .in9(b_1_b_7), .in10(b_1_b_7), .in11(b_1_b_7), .in12(b_1_b_7),
    .in13(b_1_b_4), .in14(b_1_b_8), .in15(b_1_b_8), .out(multiplexer_2_out), .sel(main_1_c_0), .en(1'b1));
  Multiplexer #(.select(4)) multiplexer_3 (
    .in0(c_1_c_1), .in1(c_1_c_2), .in2(c_1_c_3), .in3(c_1_c_4), .in4(c_1_c_5), .in5(c_1_c_5), .in6(c_1_c_6),
    .in7(c_1_c_5), .in8(c_1_c_5), .in9(c_1_c_5), .in10(c_1_c_5), .in11(c_1_c_5), .in12(c_1_c_5),
    .in13(c_1_c_5), .in14(c_1_c_6), .in15(c_1_c_7), .out(multiplexer_3_out), .sel(main_1_c_0), .en(1'b1));
  D_Flip_Flop d_ff_1 (.clk(clock_1_out), .D(multiplexer_1_out), .Q(d_ff_1_q), .en(1'b1));  // open: Qn, preset, reset
  D_Flip_Flop d_ff_2 (.clk(clock_1_out), .D(multiplexer_2_out), .Q(d_ff_2_q), .en(1'b1));  // open: Qn, preset, reset
  D_Flip_Flop d_ff_3 (.clk(clock_1_out), .D(multiplexer_3_out), .Q(d_ff_3_q), .en(1'b1));  // open: Qn, preset, reset
  // Probe on main_1_c_0
  after_mux_main main_1 (
    .CLK(clock_1_out), .top_and_1(not_1_out), .top_and_2(d_ff_1_q), .top_and_3(d_ff_2_q),
    .top_and_4(d_ff_3_q), .bot_and_1(in_1), .bot_and_2(d_ff_1_q), .bot_and_3(d_ff_3_q), .bot_and_4(d_ff_2_q),
    .C_3(main_1_c_0[3]), .C_2(main_1_c_0[2]), .C_1(main_1_c_0[1]), .C_0(main_1_c_0[0]), .OUTPUT(main_1_output));
  // Probe on main_1_output
endmodule
