// Logisim project main_logic.circ as structural Verilog: 1 circuit, main circuit main
module main (
  input  in_1,
  input  in_2,
  input  a,
  input  b,
  input  c
);

  wire and_12_out, and_13_out, and_14_out, and_15_out, and_16_out, and_17_out, and_18_out, and_19_out,
       and_20_out, and_21_out, and_22_out, and_23_out, not_1_out, not_2_out, not_3_out, not_4_out;

  not not_1 (not_1_out, in_2);
  not not_2 (not_2_out, b);
  not not_3 (not_3_out, c);
  not not_4 (not_4_out, a);
  // AND_Gate and_1 has open pins: in0=not_4_out, in1=not_2_out, in2=c, in3=in_2, out=open
  // AND_Gate and_2 has open pins: in0=b, in1=not_3_out, in2=not_1_out, out=open
  // AND_Gate and_3 has open pins: in0=b, in1=not_3_out, in2=in_2, out=open
  // AND_Gate and_4 has open pins: in0=not_2_out, in1=c, in2=in_2, out=open
  // AND_Gate and_5 has open pins: in0=not_4_out, in1=b, in2=not_3_out, in3=not_1_out, out=open
  // AND_Gate and_6 has open pins: in0=not_4_out, in1=not_2_out, in2=c, in3=not_1_out, out=open
  // AND_Gate and_7 has open pins: in0=not_4_out, in1=b, in2=c, in3=not_1_out, out=open
  // AND_Gate and_8 has open pins: in0=not_2_out, in1=c, in2=not_1_out, out=open
  // AND_Gate and_9 has open pins: in0=not_4_out, in1=not_3_out, in2=not_1_out, out=open
  // AND_Gate and_10 has open pins: in0=not_2_out, in1=not_3_out, in2=not_1_out, out=open
  // AND_Gate and_11 has open pins: in0=not_4_out, in1=not_2_out, in2=not_3_out, in3=not_1_out, out=open
  // OR_Gate or_1 has open pins: in0=and_13_out, in1=and_14_out, in2=and_15_out, in3=and_17_out, out=open
  and and_12 (and_12_out, a, not_2_out, c, in_2);
  // OR_Gate or_2 has open pins: in0=and_12_out, in1=and_17_out, in2=and_18_out, out=open
  and and_13 (and_13_out, a, b, not_3_out, not_1_out);
  and and_14 (and_14_out, a, not_2_out, not_3_out, not_1_out);
  // OR_Gate or_3 has open pins: in0=and_16_out, in1=and_15_out, in2=and_21_out, out=open
  and and_15 (and_15_out, not_4_out, b, c, not_1_out);
  // OR_Gate or_4 has open pins: in0=and_18_out, in1=and_17_out, in2=and_22_out, out=open
  and and_16 (and_16_out, a, b, not_3_out, in_2);
  // OR_Gate or_5 is placed but not wired
  and and_17 (and_17_out, a, not_2_out, c, not_1_out);
  and and_18 (and_18_out, not_4_out, b, c, in_2);
  and and_19 (and_19_out, a, not_3_out, not_1_out);
  // OR_Gate or_6 is placed but not wired
  and and_20 (and_20_out, a, not_2_out, not_3_out, not_1_out);
  and and_21 (and_21_out, a, not_2_out, not_1_out);
  // OR_Gate or_7 is placed but not wired
  // OR_Gate or_8 is placed but not wired
  and and_22 (and_22_out, a, not_3_out, in_2);
  // OR_Gate or_9 is placed but not wired
  // OR_Gate or_10 is placed but not wired
  and and_23 (and_23_out, a, not_2_out, in_2);
  // OR_Gate or_11 is placed but not wired
  // OR_Gate or_12 is placed but not wired
  // OR_Gate or_13 is placed but not wired
endmodule
